# Fritzing sketch connection_diagram_not_all_parts (saved by Fritzing 1.0.4)
circuit board: 8.46667cm x 5.64444cm

parts:
  M1 = ESP32-S3-DevKitC-1-N8R8-v1 [part_number=ESP32-S3-DevKitC-1-N8R8-v1]
  U1 = WS2812 RGB LED strip
  Part1 = Thermal Printer
  GM1 = GM67 Barcode Reader

nets:
  N1: M1.pin_4, GM1.RX
  N2: M1.pin_5, GM1.TX
  N3: M1.pin_9, Part1.RXD
  N4: M1.pin_10, Part1.TXD
  N5: M1.pin_11, U1.DOUT

custom parts:
  ESP32-S3-DevKitC-1-N8R8-v1: ESP32-S3-DevKitC-1-N8R8-v1 This module is 44pins long (2x22) and 11 pins width.
  WS2812 RGB LED strip: WS2812 strip
  GM67 Barcode Reader: Header 8 GM67 Barcode Reader V1.0. Please ignore the PCB view of this circuit it does not matter. Please feel free to make this better
